# Fritzing sketch schematic (saved by Fritzing 0.7.12b)
breadboards: 1

parts:
  Arduino1 = Arduino
  T1 = LM35 Temperature Sensor [package="TO92 [THT]"]
  U1 = LM 358 Dual Op-Amp [package="DIP8 [THT]"]
  R1 = 100k Ω Resistor [package=THT]
  R2 = 10k Ω Resistor [package=THT]

nets:
  N1: Arduino1.+5V, T1.+Vs, U1.connector7
  GND: Arduino1.GND, T1.GND, U1.connector3, R2.Pin_1
  N2: Arduino1.A0, U1.connector0, R1.Pin_0
  N3: T1.Vout, U1.connector2
  N4: U1.connector1, R1.Pin_1, R2.Pin_0
